# Fritzing sketch sketch (saved by Fritzing 0.9.3b)

parts:
  Part1 = Arduino Pro Mini (3.3V) [part_number="Pro Mini 3.3V"]
  U1 = LIPO-2000mAh [package=lipo-2000]
  Part2 = Real Time Clock Module - DS1307 RTC Breakout Board [part_number=DS1307]
  R1 = Rotary Potentiometer (Small) [maximum_resistance=10kΩ part_number="10K Poti" package=THT]
  R2 = Photocell (LDR) [part_number="Photo Resistor" package=THT]
  sdCard1 = my_sdCard [part_number=SDCard]

nets:
  GND: Part1.GND, U1.-, R1.leg1, sdCard1.GND
  N1: Part1.A4, Part2.SDA
  N2: Part1.A5, Part2.SCL
  N3: Part1.RAW, U1.+
  VCC: Part1.VCC, Part2.5V, R2.pin_1, sdCard1.VCC
  N4: Part1.SCK, sdCard1.SCK
  N5: Part1.MISO, sdCard1.MISO
  N6: Part1.MOSI, sdCard1.MOSI
  N7: Part1.D10, sdCard1.CS
  N8: Part1.D9, Part2.GND
  N9: Part1.D2, R1.wiper
  N10: R1.leg2, R2.pin_0

custom parts:
  my_sdCard: micro sdCard Adapter with 90º pin header. Use a filtering Capacitor between CS and GND if needed. PCB View Pinouts are Reversed for laying parallel on PCB using a 90º pin header.
